// Logisim project ex2_28_sop.circ as structural Verilog: 1 circuit, main circuit main
module main (
  input  A,
  input  B,
  input  C,
  input  D,
  output Y
);

  wire not_1_out, or_1_out;

  not not_1 (not_1_out, D);
  or or_1 (or_1_out, B, C, not_1_out);
  and and_1 (Y, A, or_1_out);
endmodule
