// Logisim project sumador1bit.circ as structural Verilog: 1 circuit, main circuit main
module main (
  input  A,
  input  B,
  input  Cin,
  output S,
  output Cout
);

  wire and_1_out, and_2_out, xor_1_p2, xor_1_p3, xor_1_p4;

  // XOR_Gate xor_1: pin names not known; wires that end beside it: B, xor_1_p2, xor_1_p3, xor_1_p4
  and and_1 (and_1_out, A, xor_1_p3);
  // XOR_Gate xor_2: pin names not known; wires that end beside it: xor_1_p4, Cin, S
  and and_2 (and_2_out, xor_1_p4, Cin);
  or or_1 (Cout, and_1_out, and_2_out);
endmodule
