// Logisim project sumador2bit.circ as structural Verilog: 2 circuits, main circuit main
module sumador1bit (
  input  A,
  input  B,
  input  Cin,
  output S,
  output Cout
);

  wire and_1_out, and_2_out, xor_1_p2, xor_1_p3, xor_1_p4;

  // XOR_Gate xor_1: pin names not known; wires that end beside it: B, xor_1_p2, xor_1_p3, xor_1_p4
  and and_1 (and_1_out, A, xor_1_p3);
  // XOR_Gate xor_2: pin names not known; wires that end beside it: xor_1_p4, Cin, S
  and and_2 (and_2_out, xor_1_p4, Cin);
  or or_1 (Cout, and_1_out, and_2_out);
endmodule

module main (
  input  A0,
  input  B0,
  input  Cin,
  input  A1,
  input  B1,
  output S0,
  output S1,
  output Cout
);

  wire sumador1bit_1_cout;

  sumador1bit sumador1bit_1 (.A(A0), .B(B0), .Cin(Cin), .S(S0), .Cout(sumador1bit_1_cout));
  sumador1bit sumador1bit_2 (.A(A1), .B(B1), .Cin(sumador1bit_1_cout), .S(S1), .Cout(Cout));
endmodule
